// Logisim project 4BIT SUBTRACTORmodified.circ as structural Verilog: 1 circuit, main circuit main
module main (
  input  carry,
  input  in_2,
  input  in_3,
  input  in_4,
  input  in_5,
  input  in_6,
  input  in_7,
  input  in_8,
  input  in_9,
  output out_10,
  output out_11,
  output out_12,
  output out_13,
  output carry_2
);

  wire and_1_out, and_2_out, and_3_out, and_4_out, and_5_out, and_6_out, and_7_out, and_8_out, not_1_out,
       not_2_out, not_3_out, not_4_out, not_5_out, not_6_out, not_7_out, not_8_out, or_1_out, or_2_out,
       or_3_out, xor_1_out, xor_2_out, xor_3_out, xor_4_out;

  xor xor_1 (xor_1_out, in_5, in_9);
  and and_1 (and_1_out, in_9, not_1_out);
  not not_1 (not_1_out, in_5);
  not not_2 (not_2_out, in_4);
  not not_3 (not_3_out, in_3);
  not not_4 (not_4_out, xor_1_out);
  xor xor_2 (xor_2_out, in_4, in_8);
  and and_2 (and_2_out, in_8, not_2_out);
  xor xor_3 (xor_3_out, in_3, in_7);
  and and_3 (and_3_out, in_7, not_3_out);
  xor xor_4 (xor_4_out, in_2, in_6);
  and and_4 (and_4_out, in_6, not_5_out);
  not not_5 (not_5_out, in_2);
  xor xor_5 (out_13, carry, xor_1_out);
  and and_5 (and_5_out, not_4_out, carry);
  not not_6 (not_6_out, xor_2_out);
  not not_7 (not_7_out, xor_3_out);
  not not_8 (not_8_out, xor_4_out);
  xor xor_6 (out_12, or_1_out, xor_2_out);
  and and_6 (and_6_out, not_6_out, or_1_out);
  xor xor_7 (out_11, or_2_out, xor_3_out);
  and and_7 (and_7_out, not_7_out, or_2_out);
  xor xor_8 (out_10, or_3_out, xor_4_out);
  and and_8 (and_8_out, not_8_out, or_3_out);
  or or_1 (or_1_out, and_5_out, and_1_out);
  or or_2 (or_2_out, and_6_out, and_2_out);
  or or_3 (or_3_out, and_7_out, and_3_out);
  or or_4 (carry_2, and_8_out, and_4_out);

  // Notes on the sheet:
  //   d
  //   d
  //   d
  //   d
endmodule
