// Logisim project 7Microprogram (1).circ as structural Verilog: 5 circuits, main circuit main
module main (
  input  in_1,
  input  [15:0] in_2
);

  wire clock_1_out, controls_1_clr_ac, controls_1_inc_ac, controls_1_inc_pc, controls_1_ld_ac,
       controls_1_ld_ar, controls_1_ld_dr, controls_1_ld_pc, controls_1_ld_ram;
  wire [2:0] control_memory_1_f1, control_memory_1_f2, control_memory_1_f3;
  wire [6:0] bit_extender_5_out;
  wire [7:0] bit_extender_2_out, bit_extender_3_out, bit_extender_4_out;
  wire [10:0] AR_q, DR_q, multiplexer_1_out, PC_q;
  wire [15:0] als_1_output, bit_extender_1_out, multiplexer_2_out, ram_1_data, undriven;
  wire [15:11] DR_q_2;

  Clock clock_1 (.out(clock_1_out));
  Multiplexer #(.width(11)) multiplexer_1 (.in0(PC_q), .in1(DR_q), .out(multiplexer_1_out), .sel(in_1));  // open: en
  Register #(.width(11)) AR (.D(multiplexer_1_out), .en(controls_1_ld_ar), .Q(AR_q), .clk(clock_1_out));  // open: clr
  Counter #(.width(11), .max('h7ff)) PC (
    .load(controls_1_ld_pc), .D(AR_q), .count(controls_1_inc_pc), .Q(PC_q), .clk(clock_1_out));  // open: carry, clr
  assign bit_extender_1_out = {{5{1'b0}}, PC_q};  // Bit_Extender bit_extender_1
  ALS als_1 (
    .f2(control_memory_1_f2), .f3(control_memory_1_f3), .AC(undriven), .DR({DR_q_2, DR_q}),
    .f1(control_memory_1_f1), .\output (als_1_output));  // open: in_2
  Multiplexer #(.select(2), .width(16)) multiplexer_2 (
    .in0(undriven), .in1(bit_extender_1_out), .in2(in_2), .in3(ram_1_data), .out(multiplexer_2_out));  // open: sel, en
  Register #(.width(16)) DR (
    .D(multiplexer_2_out), .en(controls_1_ld_dr), .Q({DR_q_2, DR_q}), .clk(clock_1_out));  // open: clr
  Counter #(.width(16), .max('hffff)) AC (
    .load(controls_1_ld_ac), .D(als_1_output), .count(controls_1_inc_ac), .clk(clock_1_out),
    .clr(controls_1_clr_ac));  // open: Q, carry
  RAM #(.addrWidth(11), .dataWidth(16)) ram_1 (
    .addr(AR_q), .data(ram_1_data), .clk(clock_1_out), .ld(controls_1_ld_ram));  // open: sel, clr
  assign bit_extender_2_out = {{5{1'b0}}, control_memory_1_f1};  // Bit_Extender bit_extender_2
  assign bit_extender_3_out = {{5{1'b0}}, control_memory_1_f3};  // Bit_Extender bit_extender_3
  assign bit_extender_4_out = {{5{1'b0}}, control_memory_1_f2};  // Bit_Extender bit_extender_4
  assign bit_extender_5_out = {{3{1'b0}}, DR_q_2[14:11]};  // Bit_Extender bit_extender_5
  CONTROLS controls_1 (
    .f1(bit_extender_2_out), .f2(bit_extender_4_out), .f3(bit_extender_3_out), .CLR_AC(controls_1_clr_ac),
    .INC_AC(controls_1_inc_ac), .ld_RAM(controls_1_ld_ram), .ld_AR(controls_1_ld_ar),
    .ld_AC(controls_1_ld_ac), .ld_DR(controls_1_ld_dr), .ld_PC(controls_1_ld_pc), .INC_PC(controls_1_inc_pc));
  CONTROL_MEMORY control_memory_1 (
    .MAP(bit_extender_5_out), .F3(control_memory_1_f3), .F2(control_memory_1_f2), .F1(control_memory_1_f1));  // open: in_3, in_2
endmodule

module CONTROLS (
  input  [7:0] f1,
  input  [7:0] f2,
  input  [7:0] f3,
  output CLR_AC,
  output INC_AC,
  output ld_RAM,
  output ld_AR,
  output ld_AC,
  output ld_DR,
  output ld_PC,
  output INC_PC
);

  wire or_1_out, or_3_out, or_5_out;

  or or_1 (or_1_out, f1[1], f1[4]);
  or or_2 (ld_AR, f1[5], f1[6]);
  or or_3 (or_3_out, f2[1], f2[2], f2[3]);
  or or_4 (ld_DR, f2[4], f2[5], f2[6], f2[7]);
  or or_5 (or_5_out, f3[1], f3[2], f3[3], f3[4]);
  or or_6 (ld_AC, or_1_out, or_3_out, or_5_out);

  assign CLR_AC = f1[2];
  assign INC_AC = f1[3];
  assign INC_PC = f3[5];
  assign ld_PC = f3[6];
  assign ld_RAM = f1[7];
endmodule

// IP LOGIC
module INPUT_LOGIC (
  input  [1:0] I0I1,
  input  T,
  output S0,
  output LD_SBR,
  output S1
);

  wire and_1_out, and_2_out, not_1_out;

  not not_1 (not_1_out, I0I1[1]);
  and and_1 (and_1_out, I0I1[0], I0I1[1]);
  and and_2 (and_2_out, not_1_out, T);
  and and_3 (LD_SBR, I0I1[0], not_1_out, T);
  or or_1 (S0, and_1_out, and_2_out);

  assign S1 = I0I1[1];
endmodule

// CMR
module CONTROL_MEMORY (
  input  [6:0] MAP,
  input  in_2,
  input  [6:0] in_3,
  output [2:0] F3,
  output [2:0] F2,
  output [2:0] F1
);

  wire input_logic_1_ld_sbr, multiplexer_1_out;
  wire [1:0] input_logic_1_s0, ram_1_data, ram_1_data_2;
  wire [6:0] adder_1_out, CAR_q, multiplexer_2_out, ram_1_data_3, SBR_q, undriven;

  INPUT_LOGIC input_logic_1 (
    .I0I1(ram_1_data), .T(multiplexer_1_out), .S0(input_logic_1_s0[0]), .LD_SBR(input_logic_1_ld_sbr),
    .S1(input_logic_1_s0[1]));
  Multiplexer #(.select(2)) multiplexer_1 (
    .out(multiplexer_1_out), .sel(ram_1_data_2));  // open: in0, in1, in2, in3, en
  Multiplexer #(.select(2), .width(7)) multiplexer_2 (
    .in0(adder_1_out), .in1(undriven), .in2(SBR_q), .in3(MAP), .out(multiplexer_2_out), .sel(input_logic_1_s0));  // open: en
  Register #(.width(7)) CAR (.D(multiplexer_2_out), .Q(CAR_q));  // open: en, clk, clr
  Adder #(.width(7)) adder_1 (.a(in_3), .b(CAR_q), .out(adder_1_out), .cin(in_2));  // open: cout
  RAM #(.addrWidth(7), .dataWidth(20)) ram_1 (
    .addr(CAR_q), .data({F1, F2, F3, ram_1_data_2, ram_1_data, ram_1_data_3}));  // open: sel, clk, ld, clr
  Register #(.width(7)) SBR (.D(adder_1_out), .en(input_logic_1_ld_sbr), .Q(SBR_q));  // open: clk, clr
endmodule

module ALS (
  input  [2:0] f3,
  input  [3:0] in_2,
  input  [15:0] DR,
  input  [2:0] f2,
  input  [15:0] AC,
  input  [2:0] f1,
  output [15:0] \output 
);

  wire and_1_out, and_2_out;
  wire [3:0] s0_out;
  wire [15:0] adder_1_out, and_3_out, not_1_out, or_1_out, shifter_1_out, shifter_2_out, xor_1_out;

  and and_1 (and_1_out, f3[1], f3[0]);
  or s0 (s0_out[0], f3[1], f2[1], f1[0]);
  and and_2 (and_2_out, f2[0], f2[1]);
  or s3 (s0_out[3], f3[2], and_1_out);
  or s1 (s0_out[1], f3[0], f2[0], f3[1]);
  or s2 (s0_out[2], f3[1], f3[2], and_2_out, f2[1]);
  Shifter #(.width(16)) shifter_1 (.in(DR), .\dist (in_2), .out(shifter_1_out));
  Shifter #(.width(16), .shift("lr")) shifter_2 (.in(DR), .\dist (in_2), .out(shifter_2_out));
  assign or_1_out = DR | AC;  // OR_Gate or_1, 16 bits wide
  Multiplexer #(.select(4), .width(16)) multiplexer_1 (
    .in1(adder_1_out), .in2(adder_1_out), .in4(and_3_out), .in5(or_1_out), .in6(xor_1_out), .in7(not_1_out),
    .in8(shifter_2_out), .in12(shifter_1_out), .out(\output ), .sel(s0_out));  // open: in0, in3, in9, in10, in11, in13, in14, in15, en
  assign xor_1_out = DR ^ AC;  // XOR_Gate xor_1, 16 bits wide
  assign not_1_out = ~DR;  // NOT_Gate not_1, 16 bits wide
  Adder #(.width(16)) adder_1 (.a(DR), .b(AC), .out(adder_1_out), .cin(f2[0]));  // open: cout
  assign and_3_out = DR & AC;  // AND_Gate and_3, 16 bits wide
endmodule
