// Logisim project 9(A)AssociativeMemory.circ as structural Verilog: 2 circuits, main circuit main
module main (
  input  in_1,
  input  in_2,
  input  [3:0] A,
  input  [3:0] K,
  output out_5,
  output M,
  output out_7,
  output out_8,
  output out_9
);

  wire and_1_out, and_2_out, and_3_out, and_4_out, and_5_out, and_6_out, and_7_out, and_8_out, clock_1_out,
       s_r_ff_1_q, s_r_ff_2_q, s_r_ff_3_q, s_r_ff_4_q;
  wire [3:0] counter_1_q, F;

  Counter #(.width(4), .max('hf)) counter_1 (
    .count(1'b1), .Q(counter_1_q), .clk(clock_1_out));  // open: load, D, carry, clr
  Clock clock_1 (.out(clock_1_out));
  RAM #(.addrWidth(4), .dataWidth(4)) ram_1 (.addr(counter_1_q), .data(F), .clk(clock_1_out));  // open: sel, ld, clr
  buf and_1 (and_1_out, in_2);  // AND_Gate
  buf and_2 (and_2_out, in_2);  // AND_Gate
  buf and_3 (and_3_out, in_2);  // AND_Gate
  buf and_4 (and_4_out, in_2);  // AND_Gate
  buf and_5 (and_5_out, in_2);  // AND_Gate
  buf and_6 (and_6_out, in_2);  // AND_Gate
  buf and_7 (and_7_out, in_2);  // AND_Gate
  buf and_8 (and_8_out, in_2);  // AND_Gate
  S_R_Flip_Flop s_r_ff_1 (
    .S(and_1_out), .clk(clock_1_out), .R(and_2_out), .Q(s_r_ff_1_q));  // open: Qn, preset, reset, en
  and and_9 (out_5, s_r_ff_1_q, in_1);
  S_R_Flip_Flop s_r_ff_2 (
    .S(and_3_out), .clk(clock_1_out), .R(and_4_out), .Q(s_r_ff_2_q));  // open: Qn, preset, reset, en
  and and_10 (out_7, s_r_ff_2_q, in_1);
  S_R_Flip_Flop s_r_ff_3 (
    .S(and_5_out), .clk(clock_1_out), .R(and_6_out), .Q(s_r_ff_3_q));  // open: Qn, preset, reset, en
  and and_11 (out_8, s_r_ff_3_q, in_1);
  S_R_Flip_Flop s_r_ff_4 (
    .S(and_7_out), .clk(clock_1_out), .R(and_8_out), .Q(s_r_ff_4_q));  // open: Qn, preset, reset, en
  and and_12 (out_9, s_r_ff_4_q, in_1);
  match_logic match_logic_1 (.F(F), .A(A), .K(K), .M(M));

  // Other names for the same wires on the sheet: R = in_1; W = in_2
endmodule

module match_logic (
  input  [3:0] A,
  input  [3:0] K,
  input  [3:0] F,
  output M
);

  wire and_2_out, and_3_out, and_4_out, and_5_out, and_6_out, and_7_out, and_8_out, and_9_out, not_1_out,
       not_2_out, not_3_out, not_4_out, not_5_out, not_6_out, not_7_out, not_8_out, not_9_out, not_10_out,
       not_11_out, not_12_out, X0, X1, X2, X3;

  and and_1 (M, X0, X1, X2, X3);
  not not_1 (not_1_out, F[0]);
  not not_2 (not_2_out, F[1]);
  not not_3 (not_3_out, F[2]);
  not not_4 (not_4_out, F[3]);
  not not_5 (not_5_out, A[0]);
  and and_2 (and_2_out, A[0], F[0]);
  and and_3 (and_3_out, not_5_out, not_1_out);
  not not_6 (not_6_out, K[0]);
  not not_7 (not_7_out, A[1]);
  and and_4 (and_4_out, A[1], F[1]);
  and and_5 (and_5_out, not_7_out, not_2_out);
  not not_8 (not_8_out, K[1]);
  not not_9 (not_9_out, A[2]);
  and and_6 (and_6_out, A[2], F[2]);
  and and_7 (and_7_out, not_9_out, not_3_out);
  not not_10 (not_10_out, K[2]);
  not not_11 (not_11_out, A[3]);
  and and_8 (and_8_out, A[3], F[3]);
  and and_9 (and_9_out, not_11_out, not_4_out);
  not not_12 (not_12_out, K[3]);
  or or_1 (X0, and_2_out, and_3_out, not_6_out);
  or or_2 (X1, and_4_out, and_5_out, not_8_out);
  or or_3 (X2, and_6_out, and_7_out, not_10_out);
  or or_4 (X3, and_8_out, and_9_out, not_12_out);
endmodule
