// Logisim project 9(B)CacheMemory.circ as structural Verilog: 1 circuit, main circuit main
module main (
  input  [14:0] Address,
  input  in_2,
  output out_3
);

  wire clock_1_out;
  wire [11:0] ram_1_data, ram_2_data;
  wire [14:0] counter_1_q, multiplexer_1_out;

  Counter #(.width(15), .max('h7fff)) counter_1 (
    .count(1'b1), .Q(counter_1_q), .clk(clock_1_out));  // open: load, D, carry, clr
  Clock clock_1 (.out(clock_1_out));
  Multiplexer #(.width(15), .enable("false")) multiplexer_1 (
    .in0(Address), .in1(counter_1_q), .out(multiplexer_1_out), .sel(in_2));
  RAM #(.addrWidth(15), .dataWidth(12)) ram_1 (
    .addr(multiplexer_1_out), .data(ram_1_data), .clk(clock_1_out));  // open: sel, ld, clr
  RAM #(.addrWidth(9), .dataWidth(12)) ram_2 (
    .addr(Address[8:0]), .data(ram_2_data), .clk(clock_1_out));  // open: sel, ld, clr
  Comparator #(.width(12)) comparator_1 (.a(ram_1_data), .b(ram_2_data), .eq(out_3));  // open: gt, lt

  // Other names for the same wires on the sheet: Index[8:0] = Address[8:0]; Tag[5:0] = Address[14:9]

  // Notes on the sheet:
  //   Main Memory
  //   Cache Memory
endmodule
