// Logisim project ALS.circ as structural Verilog: 1 circuit, main circuit main
module main (
  output [3:0] out_1,
  output [3:0] _11__Shl
);

  wire clock_1_out;
  wire [2:0] shifter_6_out;
  wire [3:0] adder_1_out, adder_2_out, and_1_out, multiplexer_1_out, not_1_out, or_1_out, shifter_1_out,
       shifter_2_out, shifter_3_out, shifter_4_out, shifter_5_out, subtractor_1_out, subtractor_2_out,
       undriven, xor_1_out;

  assign and_1_out = out_1 & _11__Shl;  // AND_Gate and_1, 4 bits wide
  assign or_1_out = out_1 | _11__Shl;  // OR_Gate or_1, 4 bits wide
  assign xor_1_out = out_1 ^ _11__Shl;  // XOR_Gate xor_1, 4 bits wide
  assign not_1_out = ~out_1;  // NOT_Gate not_1, 4 bits wide
  Adder #(.width(4)) adder_1 (.a(out_1), .b(_11__Shl), .out(adder_1_out));  // open: cin, cout
  Subtractor #(.width(4)) subtractor_1 (.a(out_1), .b(_11__Shl), .out(subtractor_1_out));  // open: bin, bout
  Adder #(.width(4)) adder_2 (.a(out_1), .b(4'b0001), .out(adder_2_out));  // open: cin, cout
  Subtractor #(.width(4)) subtractor_2 (.a(out_1), .b(4'b0001), .out(subtractor_2_out));  // open: bin, bout
  Shifter #(.width(4), .shift("lr")) shifter_1 (.in(out_1), .\dist (2'b01), .out(shifter_1_out));
  Shifter #(.width(4)) shifter_2 (.in(out_1), .\dist (2'b01), .out(shifter_2_out));
  Shifter #(.width(4), .shift("rr")) shifter_3 (.in(out_1), .\dist (2'b01), .out(shifter_3_out));
  Shifter #(.width(4), .shift("rl")) shifter_4 (.in(out_1), .\dist (2'b01), .out(shifter_4_out));
  Shifter #(.width(4), .shift("ar")) shifter_5 (.in(out_1), .\dist (2'b01), .out(shifter_5_out));
  Shifter #(.width(3)) shifter_6 (.in(out_1[2:0]), .\dist (2'b01), .out(shifter_6_out));
  Multiplexer #(.select(4), .width(4)) multiplexer_1 (
    .in0(out_1), .in1(_11__Shl), .in2(and_1_out), .in3(or_1_out), .in4(xor_1_out), .in5(not_1_out),
    .in6(adder_1_out), .in7(subtractor_1_out), .in8(adder_2_out), .in9(subtractor_2_out),
    .in10(shifter_1_out), .in11(shifter_2_out), .in12(shifter_3_out), .in13(shifter_4_out),
    .in14(shifter_5_out), .in15({out_1[3], shifter_6_out}), .out(multiplexer_1_out), .sel(undriven));  // open: en
  Register #(.width(4)) register_1 (.D(multiplexer_1_out), .Q(out_1), .clk(clock_1_out));  // open: en, clr
  Register #(.width(4)) register_2 (.Q(_11__Shl), .clk(clock_1_out));  // open: D, en, clr
  Register #(.width(4)) register_3 (.D(undriven), .clk(clock_1_out));  // open: en, Q, clr
  Clock clock_1 (.out(clock_1_out));

  // Notes on the sheet:
  //    AC
  //   DR
  //   0. Transfer AC
  //   1. Transfer  DR
  //   2. AND
  //   3. OR
  //   4. XOR
  //   5. NOT
  //   6. Adder
  //   7. Subtracter
  //   8. Increment
  //   9. Decrement
  //   10. Shr
  //   12. Cir
  //   13. Cil
  //   14. Ashr
  //   15. ashl
endmodule
