// Logisim project AddersSubtracter.circ as structural Verilog: 1 circuit, main circuit main
module main (
  input  in_1,
  input  in_2,
  input  in_3,
  input  in_4,
  input  in_5,
  input  in_6,
  input  in_7,
  input  in_8,
  input  in_9,
  input  in_10,
  input  in_11
);

  wire adder_1_cout, adder_1_out, clock_1_out, d_ff_1_q, not_1_out, shift_register_1_out,
       shift_register_2_out, xor_1_out, xor_2_out;

  Clock clock_1 (.out(clock_1_out));
  not not_1 (not_1_out, in_9);
  Shift_Register #(.length(4)) shift_register_1 (
    .shift(in_9), .in(xor_2_out), .clk(clock_1_out), .out(shift_register_1_out), .load(not_1_out), .d0(in_1),
    .d1(in_2), .d2(in_3), .d3(in_4));  // open: clr, q0, q1, q2, q3
  Shift_Register #(.length(4)) shift_register_2 (
    .shift(in_9), .in(in_10), .clk(clock_1_out), .out(shift_register_2_out), .load(not_1_out), .d0(in_5),
    .d1(in_6), .d2(in_7), .d3(in_8));  // open: clr, q0, q1, q2, q3
  xor xor_1 (xor_1_out, shift_register_2_out, in_11);
  Adder #(.width(1)) adder_1 (
    .a(shift_register_1_out), .b(xor_1_out), .out(adder_1_out), .cin(d_ff_1_q), .cout(adder_1_cout));
  D_Flip_Flop d_ff_1 (.clk(clock_1_out), .D(adder_1_cout), .Q(d_ff_1_q));  // open: Qn, preset, en, reset
  xor xor_2 (xor_2_out, adder_1_out, in_11);
endmodule
