// Logisim project Basic(andaddbunski).circ as structural Verilog: 1 circuit, main circuit main
module main (
  input  in_1,
  input  [2:0] in_2,
  input  [15:0] in_3,
  output [11:0] AR_op,
  output [11:0] PC_op,
  output [15:0] IR_op,
  output E
);

  wire adder_1_cout, bitselector_1_out, Clock_out, T0, T1, T2, T3, T4, T5, undriven, undriven_2;
  wire [1:1] or_1_out;
  wire [2:0] bitselector_2_out;
  wire [3:0] counter_1_q;
  wire [11:0] BUS_out_12;
  wire [15:0] AC_op, adder_1_out, and_1_out, bit_extender_1_out, bit_extender_2_out, BUS_out_16, DR_op,
       M_out, multiplexer_2_out, register_1_q;

  Clock Clock (.out(Clock_out));
  Counter #(.width(4), .max('hf)) counter_1 (
    .Q(counter_1_q), .clk(Clock_out), .clr(T2));  // open: load, D, count, carry
  Register #(.width(12)) AR (.D(BUS_out_12), .en(T0), .Q(AR_op), .clk(Clock_out), .clr(in_1));
  Counter #(.width(12), .max('hfff)) PC (
    .D(BUS_out_12), .count(T1), .Q(PC_op), .clk(Clock_out), .clr(in_1));  // open: load, carry
  Register #(.width(16)) IR (.D(BUS_out_16), .en(T1), .Q(IR_op), .clk(Clock_out), .clr(in_1));
  Register #(.width(16)) DR (.D(BUS_out_16), .en(T4), .Q(DR_op), .clk(Clock_out));  // open: clr
  Register #(.width(16)) AC (.D(in_3), .en(undriven), .Q(AC_op), .clk(Clock_out));  // open: clr
  assign bit_extender_1_out = {{4{1'b0}}, AR_op};  // Bit_Extender bit_extender_1
  assign bit_extender_2_out = {{4{1'b0}}, PC_op};  // Bit_Extender bit_extender_2
  BitSelector #(.width(16)) bitselector_1 (.in(IR_op), .out(bitselector_1_out), .sel(4'b0001));
  BitSelector #(.width(16), .group(3)) bitselector_2 (.in(IR_op), .out(bitselector_2_out), .sel(in_2));
  BitSelector #(.width(16), .group(12)) bitselector_3 (.in(IR_op), .out(BUS_out_12), .sel(1'b0));
  Decoder #(.select(4)) decoder_1 (
    .out0(T0), .out1(T1), .out2(T2), .out3(T3), .out4(T4), .out5(T5), .sel(counter_1_q));  // open: out6, out7, out8, out9, out10, out11, out12, out13, out14, out15, en
  D_Flip_Flop I (.clk(Clock_out), .D(bitselector_1_out));  // open: Q, Qn, preset, en, reset
  ROM #(.addrWidth(12), .dataWidth(16)) rom_1 (.addr(AR_op), .data(M_out));  // open: sel
  Decoder #(.select(3), .enable("false")) decoder_2 (.sel(bitselector_2_out));  // open: out0, out1, out2, out3, out4, out5, out6, out7
  or or_1 (or_1_out[1], T0, T1);
  Multiplexer #(.select(3), .width(16), .enable("false")) multiplexer_1 (
    .in1(bit_extender_1_out), .in2(bit_extender_2_out), .in3(DR_op), .in4(AC_op), .in5(IR_op), .in7(M_out),
    .out(BUS_out_16), .sel({T1, or_1_out[1], T1}));  // open: in0, in6
  Bit_Extender #(.in_width(16), .out_width(12)) bit_extender_3 (.in(BUS_out_16), .out(BUS_out_12));
  Register #(.width(16)) register_1 (.D(AC_op), .Q(register_1_q), .clk(Clock_out));  // open: en, clr
  assign and_1_out = register_1_q & DR_op;  // AND_Gate and_1, 16 bits wide
  Adder #(.width(16)) adder_1 (.a(register_1_q), .b(DR_op), .out(adder_1_out), .cin(E), .cout(adder_1_cout));
  D_Flip_Flop d_ff_1 (.clk(Clock_out), .D(adder_1_cout), .Q(E));  // open: Qn, preset, en, reset
  Multiplexer #(.width(16), .enable("false")) multiplexer_2 (
    .in0(and_1_out), .in1(adder_1_out), .out(multiplexer_2_out), .sel(undriven_2));

  // Notes on the sheet:
  //   contents of rom_1 (hex, n*v repeats v):
  //   52 4254 2212 1232 422 453 542 564 4645 3 5434 78 7 8787 8 78 8878 878 87 78 0 778 878 878 87 8 7 87
  //   878 78 78 7 6345 15*0 4532 15*0 5344 15*0 6746 154*0 6868
endmodule
