// Logisim project Fetchcycle.circ as structural Verilog: 1 circuit, main circuit main
module main (
  input  [3:0] in_1,
  input  in_2,
  output [15:0] out_3
);

  wire clock_1_out, decoder_1_out0, decoder_1_out1;
  wire [3:0] counter_1_q;
  wire [11:0] adder_1_out, register_1_q, register_2_q;
  wire [15:0] rom_1_data;

  Clock clock_1 (.out(clock_1_out));
  Register #(.width(12)) register_1 (
    .D(register_2_q), .en(decoder_1_out0), .Q(register_1_q), .clk(clock_1_out));  // open: clr
  Register #(.width(12)) register_2 (
    .D(adder_1_out), .en(decoder_1_out1), .Q(register_2_q), .clk(clock_1_out));  // open: clr
  Register #(.width(16)) register_3 (.D(rom_1_data), .en(decoder_1_out1), .Q(out_3), .clk(clock_1_out));  // open: clr
  Counter #(.width(4), .max('hf)) counter_1 (
    .D(in_1), .Q(counter_1_q), .clk(clock_1_out), .clr(in_2));  // open: load, count, carry
  ROM #(.addrWidth(12), .dataWidth(16)) rom_1 (.addr(register_1_q), .data(rom_1_data));  // open: sel
  Decoder #(.select(4)) decoder_1 (
    .out0(decoder_1_out0), .out1(decoder_1_out1), .sel(counter_1_q));  // open: out2, out3, out4, out5, out6, out7, out8, out9, out10, out11, out12, out13, out14, out15, en
  Adder #(.width(12)) adder_1 (.a(register_2_q), .b(12'h1), .out(adder_1_out));  // open: cin, cout

  // Notes on the sheet:
  //   AR
  //   PC
  //   IR
  //   contents of rom_1 (hex, n*v repeats v):
  //   1
endmodule
