// Logisim project Parallel.circ as structural Verilog: 1 circuit, main circuit main
module main (
  input  in_1,
  input  in_2,
  input  [1:0] in_3,
  input  [1:0] in_4
);

  wire clock_1_out, decoder_1_out0, decoder_1_out1, decoder_1_out2, decoder_1_out3, multiplexer_1_out,
       multiplexer_2_out, multiplexer_3_out, multiplexer_4_out, shift_register_1_q0, shift_register_1_q1,
       shift_register_1_q2, shift_register_1_q3, shift_register_2_q0, shift_register_2_q1,
       shift_register_2_q2, shift_register_2_q3, shift_register_3_q0, shift_register_3_q1,
       shift_register_3_q2, shift_register_3_q3, shift_register_4_q0, shift_register_4_q1,
       shift_register_4_q2, shift_register_4_q3;

  Clock clock_1 (.out(clock_1_out));
  Decoder #(.select(2)) decoder_1 (
    .out0(decoder_1_out0), .out1(decoder_1_out1), .out2(decoder_1_out2), .out3(decoder_1_out3), .sel(in_3),
    .en(in_2));
  Shift_Register #(.length(4)) shift_register_1 (
    .shift(in_1), .clk(clock_1_out), .load(decoder_1_out0), .d0(multiplexer_1_out), .q0(shift_register_1_q0),
    .d1(multiplexer_2_out), .q1(shift_register_1_q1), .d2(multiplexer_3_out), .q2(shift_register_1_q2),
    .d3(multiplexer_4_out), .q3(shift_register_1_q3));  // open: in, out, clr
  Multiplexer #(.select(2), .enable("false")) multiplexer_1 (
    .in0(shift_register_1_q0), .in1(shift_register_2_q0), .in2(shift_register_3_q0),
    .in3(shift_register_4_q0), .out(multiplexer_1_out), .sel(in_4));
  Shift_Register #(.length(4)) shift_register_2 (
    .shift(in_1), .clk(clock_1_out), .load(decoder_1_out1), .d0(multiplexer_1_out), .q0(shift_register_2_q0),
    .d1(multiplexer_2_out), .q1(shift_register_2_q1), .d2(multiplexer_3_out), .q2(shift_register_2_q2),
    .d3(multiplexer_4_out), .q3(shift_register_2_q3));  // open: in, out, clr
  Multiplexer #(.select(2), .enable("false")) multiplexer_2 (
    .in0(shift_register_1_q1), .in1(shift_register_2_q1), .in2(shift_register_3_q1),
    .in3(shift_register_4_q1), .out(multiplexer_2_out), .sel(in_4));
  Shift_Register #(.length(4)) shift_register_3 (
    .shift(in_1), .clk(clock_1_out), .load(decoder_1_out2), .d0(multiplexer_1_out), .q0(shift_register_3_q0),
    .d1(multiplexer_2_out), .q1(shift_register_3_q1), .d2(multiplexer_3_out), .q2(shift_register_3_q2),
    .d3(multiplexer_4_out), .q3(shift_register_3_q3));  // open: in, out, clr
  Multiplexer #(.select(2), .enable("false")) multiplexer_3 (
    .in0(shift_register_1_q2), .in1(shift_register_2_q2), .in2(shift_register_3_q2),
    .in3(shift_register_4_q2), .out(multiplexer_3_out), .sel(in_4));
  Shift_Register #(.length(4)) shift_register_4 (
    .shift(in_1), .clk(clock_1_out), .load(decoder_1_out3), .d0(multiplexer_1_out), .q0(shift_register_4_q0),
    .d1(multiplexer_2_out), .q1(shift_register_4_q1), .d2(multiplexer_3_out), .q2(shift_register_4_q2),
    .d3(multiplexer_4_out), .q3(shift_register_4_q3));  // open: in, out, clr
  Multiplexer #(.select(2), .enable("false")) multiplexer_4 (
    .in0(shift_register_1_q3), .in1(shift_register_2_q3), .in2(shift_register_3_q3),
    .in3(shift_register_4_q3), .out(multiplexer_4_out), .sel(in_4));
endmodule
