// Logisim project Stack.circ as structural Verilog: 1 circuit, main circuit main
module main (
  input  [3:0] in_1,
  input  in_2,
  output [3:0] out_3,
  output Overflow,
  output Underflow
);

  wire clock_1_out, counter_1_carry, d_ff_1_q, d_ff_2_q, nor_1_out, not_1_out;
  wire [2:0] counter_1_q;

  Clock clock_1 (.out(clock_1_out));
  Counter #(.width(3), .max('h7)) counter_1 (
    .load(in_2), .count(nor_1_out), .Q(counter_1_q), .carry(counter_1_carry), .clk(clock_1_out));  // open: D, clr
  not not_1 (not_1_out, in_2);
  D_Flip_Flop d_ff_1 (.clk(clock_1_out), .D(counter_1_carry), .Q(d_ff_1_q));  // open: Qn, preset, en, reset
  D_Flip_Flop d_ff_2 (.clk(clock_1_out), .D(counter_1_carry), .Q(d_ff_2_q));  // open: Qn, preset, en, reset
  RAM #(.addrWidth(3), .dataWidth(4), .bus("separate")) ram_1 (
    .addr(counter_1_q), .din(in_1), .data(out_3), .str(not_1_out), .clk(clock_1_out), .ld(in_2));  // open: sel, clr
  and and_1 (Overflow, not_1_out, d_ff_1_q);
  and and_2 (Underflow, in_2, d_ff_2_q);
  nor nor_1 (nor_1_out, Overflow, Underflow);

  // Notes on the sheet:
  //   StackPointer
  //   RAM
endmodule
