// Logisim project basicALSU.circ as structural Verilog: 1 circuit, main circuit main
module main (
  input  [3:0] in_1,
  input  [3:0] in_2,
  input  [1:0] in_3,
  input  [1:0] in_4,
  input  [1:0] in_5,
  input  [1:0] in_6,
  input  in_7,
  output [3:0] out_8,
  output [3:0] out_9,
  output [3:0] out_10,
  output [3:0] out_11
);

  wire multiplexer_1_out, multiplexer_2_out, multiplexer_3_out, xor_1_out, xor_2_out;
  wire [3:0] and_1_out, multiplexer_4_out, not_1_out, not_2_out, or_1_out, xor_3_out;

  xor xor_1 (xor_1_out, in_1[3], in_1[2]);
  xor xor_2 (xor_2_out, xor_1_out, in_1[2]);
  assign not_1_out = ~in_2;  // NOT_Gate not_1, 4 bits wide
  Multiplexer #(.select(2)) multiplexer_1 (
    .in0(1'b0), .in1(in_1[0]), .in2(in_1[3]), .out(multiplexer_1_out), .sel(in_6));  // open: in3, en
  Multiplexer multiplexer_2 (.in0(in_1[2]), .in1(xor_2_out), .out(multiplexer_2_out), .sel(in_6[1]));  // open: en
  Multiplexer multiplexer_3 (.in0(1'b0), .in1(in_1[3]), .out(multiplexer_3_out), .sel(in_6[0]));  // open: en
  Multiplexer #(.select(2), .width(4)) multiplexer_4 (
    .in0(in_2), .in1(4'b0000), .in2(4'b1111), .in3(not_1_out), .out(multiplexer_4_out), .sel(in_3));  // open: en
  assign and_1_out = in_1 & in_2;  // AND_Gate and_1, 4 bits wide
  assign or_1_out = in_1 | in_2;  // OR_Gate or_1, 4 bits wide
  assign xor_3_out = in_1 ^ in_2;  // XOR_Gate xor_3, 4 bits wide
  assign not_2_out = ~in_1;  // NOT_Gate not_2, 4 bits wide
  Multiplexer multiplexer_5 (
    .in0(multiplexer_1_out), .in1(multiplexer_2_out), .out(out_11[3]), .sel(in_7));  // open: en
  Multiplexer multiplexer_6 (.in0(in_1[3]), .in1(in_1[1]), .out(out_11[2]), .sel(in_7));  // open: en
  Multiplexer multiplexer_7 (.in0(in_1[2]), .in1(in_1[0]), .out(out_11[1]), .sel(in_7));  // open: en
  Multiplexer multiplexer_8 (.in0(in_1[1]), .in1(multiplexer_3_out), .out(out_11[0]), .sel(in_7));  // open: en
  Adder #(.width(4)) adder_1 (.a(in_1), .b(multiplexer_4_out), .out(out_8), .cin(in_3[0]));  // open: cout
  Multiplexer #(.select(2), .width(4)) multiplexer_9 (
    .in0(and_1_out), .in1(or_1_out), .in2(xor_3_out), .in3(not_2_out), .out(out_9), .sel(in_5));  // open: en
  Multiplexer #(.select(2), .width(4)) multiplexer_10 (
    .in0(out_8), .in1(out_9), .in2(out_11), .out(out_10), .sel(in_4));  // open: in3, en
endmodule
